// Logisim project 6.circ as structural Verilog: 1 circuit, main circuit main
module main (
);

  wire a, and_1_out, and_2_out, and_3_out, and_4_out, and_5_out, and_6_out, and_7_out, and_8_out, and_9_out,
       and_10_out, b, c, clock_1_out, go, not_1_out, not_2_out, not_3_out, not_4_out, not_5_out, not_6_out,
       Reset_out, t_ff_1_q, t_ff_2_q, t_ff_3_q, w0, w1, w2, w3;

  Clock clock_1 (.out(clock_1_out));
  // Probe on a
  // Probe on {w3, w2, w1, w0}
  // Probe on b
  // Probe on c
  T_Flip_Flop t_ff_1 (.clk(clock_1_out), .T(1'b1), .Q(t_ff_1_q), .Qn(w0), .preset(Reset_out), .en(go));  // open: reset
  nand nand_1 (go, not_1_out, w1, not_2_out, w3);
  T_Flip_Flop t_ff_2 (.clk(t_ff_1_q), .T(1'b1), .Q(t_ff_2_q), .Qn(w1), .preset(Reset_out));  // open: reset, en
  not not_1 (not_1_out, w0);
  not not_2 (not_2_out, w2);
  TTY #(.rows(1), .cols(18)) tty_1 (.data({6'b011000, a}), .clk(clock_1_out), .we(go), .clr(Reset_out));
  TTY #(.rows(1), .cols(18)) tty_2 (.data({6'b011000, b}), .clk(clock_1_out), .we(go), .clr(Reset_out));
  TTY #(.rows(1), .cols(18)) tty_3 (.data({6'b011000, c}), .clk(clock_1_out), .we(go), .clr(Reset_out));
  T_Flip_Flop t_ff_3 (.clk(t_ff_2_q), .T(1'b1), .Q(t_ff_3_q), .Qn(w2), .preset(Reset_out));  // open: reset, en
  T_Flip_Flop t_ff_4 (.clk(t_ff_3_q), .T(1'b1), .Qn(w3), .preset(Reset_out));  // open: Q, reset, en
  Button Reset (.out(Reset_out));
  not not_3 (not_3_out, w3);
  not not_4 (not_4_out, w1);
  not not_5 (not_5_out, w2);
  not not_6 (not_6_out, w0);
  and and_1 (and_1_out, w2, w0);
  buf and_2 (and_2_out, w3);  // AND_Gate
  buf and_3 (and_3_out, w1);  // AND_Gate
  and and_4 (and_4_out, not_5_out, not_6_out);
  buf and_5 (and_5_out, not_5_out);  // AND_Gate
  and and_6 (and_6_out, not_4_out, not_6_out);
  and and_7 (and_7_out, w1, w0);
  buf and_8 (and_8_out, w2);  // AND_Gate
  buf and_9 (and_9_out, not_4_out);  // AND_Gate
  buf and_10 (and_10_out, w0);  // AND_Gate
  or or_1 (a, and_1_out, and_2_out, and_3_out, and_4_out);
  or or_2 (b, and_5_out, and_6_out, and_7_out);
  or or_3 (c, and_8_out, and_9_out, and_10_out);

  // Notes on the sheet:
  //   1011011111
  //   1111100111
  //   1101111111
  //   go until 10
endmodule
