// Logisim project 7.circ as structural Verilog: 1 circuit, main circuit main
module main (
);

  wire A0, A1, A2, C0, C1, C2, C3, clock_1_out, D0, D1, D2, D3, D4, D5, D6, D7, decoder_1_out3,
       decoder_1_out5, decoder_1_out6, decoder_1_out7, decoder_1_out9, decoder_1_out10, decoder_1_out11,
       decoder_1_out12, go, newC1_out, newC2_out, newC3_out, P0, P1, P2, Reset_out, t_ff_1_q, t_ff_2_q,
       t_ff_3_q, t_ff_4_q, t_ff_5_q, t_ff_6_q, xor_1_out, Z0, Z1, Z2, Z3, Z4, Z5, Z6, Z7;
  wire [0:0] multiplexer_1_out;
  wire [3:0] xor_2_out;

  ExactlyOne xor_1 (.out(xor_1_out), .in0(D0), .in1(D1), .in2(D3), .in3(D4), .in4(D6));
  ExactlyOne newC1 (.out(newC1_out), .in0(D0), .in1(D2), .in2(D3), .in3(D5), .in4(D6));
  ExactlyOne newC2 (.out(newC2_out), .in0(D1), .in1(D2), .in2(D3), .in3(D7));
  ExactlyOne newC3 (.out(newC3_out), .in0(D4), .in1(D5), .in2(D6), .in3(D7));
  xor xor_2 (xor_2_out[0], C0, xor_1_out);
  xor xor_3 (xor_2_out[1], C1, newC1_out);
  xor xor_4 (xor_2_out[2], C2, newC2_out);
  xor xor_5 (xor_2_out[3], C3, newC3_out);
  Decoder #(.select(4)) decoder_1 (
    .out3(decoder_1_out3), .out5(decoder_1_out5), .out6(decoder_1_out6), .out7(decoder_1_out7),
    .out9(decoder_1_out9), .out10(decoder_1_out10), .out11(decoder_1_out11), .out12(decoder_1_out12),
    .sel(xor_2_out));  // open: out0, out1, out2, out4, out8, out13, out14, out15, en
  xor xor_6 (Z0, decoder_1_out3, D0);
  xor xor_7 (Z1, decoder_1_out5, D1);
  xor xor_8 (Z2, decoder_1_out6, D2);
  xor xor_9 (Z3, decoder_1_out7, D3);
  xor xor_10 (Z4, decoder_1_out9, D4);
  xor xor_11 (Z5, decoder_1_out10, D5);
  xor xor_12 (Z6, decoder_1_out11, D6);
  xor xor_13 (Z7, decoder_1_out12, D7);
  Clock clock_1 (.out(clock_1_out));
  T_Flip_Flop t_ff_1 (.clk(clock_1_out), .T(1'b1), .Q(t_ff_1_q), .Qn(P0), .preset(Reset_out), .en(go));  // open: reset
  Multiplexer #(.select(3), .disabled(0), .enable("false")) multiplexer_1 (
    .in0(Z7), .in1(Z6), .in2(Z5), .in3(Z4), .in4(Z3), .in5(Z2), .in6(Z1), .in7(Z0),
    .out(multiplexer_1_out[0]), .sel({P2, P1, P0}));
  T_Flip_Flop t_ff_2 (.clk(t_ff_1_q), .T(1'b1), .Q(t_ff_2_q), .Qn(P1), .preset(Reset_out));  // open: reset, en
  TTY #(.cols(8)) tty_1 (.data({6'b011000, multiplexer_1_out[0]}), .clk(clock_1_out), .we(go), .clr(Reset_out));
  T_Flip_Flop t_ff_3 (.clk(t_ff_4_q), .T(1'b1), .Q(t_ff_3_q), .Qn(A0), .preset(Reset_out));  // open: reset, en
  T_Flip_Flop t_ff_4 (.clk(t_ff_2_q), .T(1'b1), .Q(t_ff_4_q), .Qn(P2), .preset(Reset_out));  // open: reset, en
  // Probe on {D7, D6, D5, D4, C3, D3, D2, D1, C2, D0, C1, C0}
  ROM #(.addrWidth(3), .dataWidth(12)) rom_1 (
    .addr({A2, A1, A0}), .data({D7, D6, D5, D4, C3, D3, D2, D1, C2, D0, C1, C0}));  // open: sel
  T_Flip_Flop t_ff_5 (.clk(t_ff_3_q), .T(1'b1), .Q(t_ff_5_q), .Qn(A1), .preset(Reset_out));  // open: reset, en
  T_Flip_Flop t_ff_6 (.clk(t_ff_5_q), .T(1'b1), .Q(t_ff_6_q), .Qn(A2), .preset(Reset_out));  // open: reset, en
  T_Flip_Flop t_ff_7 (.clk(t_ff_6_q), .T(1'b1), .Q(go), .preset(Reset_out));  // open: Qn, reset, en
  Button Reset (.out(Reset_out));

  // Notes on the sheet:
  //   12   11  10  9    8    7     6     5     4    3    2     1 
  //   contents of rom_1 (hex, n*v repeats v):
  //   d7 788 a75 a74 275 b75 f75 a77
  //   00101011
  //   01110000
  //   10101111
  //   10101111
  //   10101111
  //   10101111
  //   11111111
  //   10101111
endmodule
