// Logisim project 1test.circ as structural Verilog: 1 circuit, main circuit main
module main (
  input  in_1
);

  wire _15, _30, CLOCK, clock_1_out, counter_2_carry, not_1_out, Reset_out, xor_1_out, xor_2_out;
  wire [7:0] counter_1_q, counter_3_q;

  xor xor_1 (xor_1_out, _30, in_1);
  D_Flip_Flop d_ff_1 (.clk(CLOCK), .D(xor_1_out), .Q(_30));  // open: Qn, preset, en, reset
  // Probe on counter_1_q
  Counter counter_1 (.Q(counter_1_q), .clk(_30));  // open: load, D, count, carry, clr
  Counter counter_2 (.carry(counter_2_carry), .clk(CLOCK), .clr(Reset_out));  // open: load, D, count, Q
  and and_1 (CLOCK, clock_1_out, not_1_out);
  Clock clock_1 (.out(clock_1_out));
  xor xor_2 (xor_2_out, in_1, _15);
  // Probe on counter_3_q
  Counter counter_3 (.Q(counter_3_q), .clk(_15));  // open: load, D, count, carry, clr
  not not_1 (not_1_out, counter_2_carry);
  D_Flip_Flop d_ff_2 (.clk(_30), .D(xor_2_out), .Q(_15));  // open: Qn, preset, en, reset
  Button Reset (.out(Reset_out));

  // Notes on the sheet:
  //   1 0 0 0 00 0 0
  //   0 1 0 0 0 0 0 0
endmodule
