// Logisim project 4test.circ as structural Verilog: 1 circuit, main circuit main
module main (
);

  wire and_1_out, and_2_out, and_3_out, and_5_out, and_6_out, and_7_out, and_8_out, and_9_out, and_10_out,
       and_11_out, and_12_out, Carry, CLK, clock_1_out, counter_1_carry, D0, D1, D2, D3, Enable, Load,
       multiplexer_1_out, multiplexer_2_out, multiplexer_3_out, multiplexer_4_out, not_1_out, not_2_out,
       not_3_out, not_4_out, not_5_out, or_1_out, or_2_out, or_3_out, or_4_out, Q0, Q1, Q2, Q3, t_ff_1_qn,
       t_ff_2_qn, t_ff_3_qn, t_ff_4_qn, xor_1_out, xor_2_out, xor_3_out, xor_4_out;
  wire [5:1] counter_1_q;

  and and_1 (and_1_out, Enable, Q0);
  and and_2 (and_2_out, and_1_out, Q1);
  and and_3 (and_3_out, and_2_out, Q3);
  and and_4 (Carry, and_3_out, Q3);
  xor xor_1 (xor_1_out, Q0, Enable);
  xor xor_2 (xor_2_out, Q1, and_1_out);
  xor xor_3 (xor_3_out, Q2, and_2_out);
  xor xor_4 (xor_4_out, Q3, and_3_out);
  Multiplexer multiplexer_1 (.in0(xor_1_out), .in1(D0), .out(multiplexer_1_out), .sel(Load));  // open: en
  not not_1 (not_1_out, multiplexer_1_out);
  Multiplexer multiplexer_2 (.in0(xor_2_out), .in1(D1), .out(multiplexer_2_out), .sel(Load));  // open: en
  not not_2 (not_2_out, multiplexer_2_out);
  Multiplexer multiplexer_3 (.in0(xor_3_out), .in1(D2), .out(multiplexer_3_out), .sel(Load));  // open: en
  not not_3 (not_3_out, multiplexer_3_out);
  Multiplexer multiplexer_4 (.in0(xor_4_out), .in1(D3), .out(multiplexer_4_out), .sel(Load));  // open: en
  not not_4 (not_4_out, multiplexer_4_out);
  and and_5 (and_5_out, t_ff_1_qn, multiplexer_1_out);
  and and_6 (and_6_out, not_1_out, Q0);
  and and_7 (and_7_out, t_ff_2_qn, multiplexer_2_out);
  and and_8 (and_8_out, not_2_out, Q1);
  and and_9 (and_9_out, t_ff_3_qn, multiplexer_3_out);
  and and_10 (and_10_out, not_3_out, Q2);
  and and_11 (and_11_out, t_ff_4_qn, multiplexer_4_out);
  and and_12 (and_12_out, not_4_out, Q3);
  or or_1 (or_1_out, and_5_out, and_6_out);
  or or_2 (or_2_out, and_7_out, and_8_out);
  or or_3 (or_3_out, and_9_out, and_10_out);
  or or_4 (or_4_out, and_11_out, and_12_out);
  T_Flip_Flop t_ff_1 (.clk(CLK), .T(or_1_out), .Q(Q0), .Qn(t_ff_1_qn));  // open: preset, reset, en
  T_Flip_Flop t_ff_2 (.clk(CLK), .T(or_2_out), .Q(Q1), .Qn(t_ff_2_qn));  // open: preset, reset, en
  T_Flip_Flop t_ff_3 (.clk(CLK), .T(or_3_out), .Q(Q2), .Qn(t_ff_3_qn));  // open: preset, reset, en
  T_Flip_Flop t_ff_4 (.clk(CLK), .T(or_4_out), .Q(Q3), .Qn(t_ff_4_qn));  // open: preset, reset, en
  Counter #(.width(6), .max('h24)) counter_1 (
    .Q({counter_1_q[5], Load, D3, counter_1_q[2:1], D0}), .carry(counter_1_carry), .clk(CLK));  // open: load, D, count, clr
  and and_13 (CLK, clock_1_out, not_5_out);
  not not_5 (not_5_out, counter_1_carry);
  Clock clock_1 (.out(clock_1_out));
  TTY #(.rows(1), .cols(37)) tty_1 (.data({2'b10, Carry, Q3, Q2, Q1, Q0}), .clk(CLK));  // open: we, clr
  or or_5 (D1, Enable, counter_1_q[1]);
  not not_6 (Enable, counter_1_q[5]);
  or or_6 (D2, counter_1_q[2], Load);

  // Notes on the sheet:
  //   @ABCDEFGHIJKLMN_@FGFGFGFGN_N_N_N0000
endmodule
