// Logisim project Brown7.9.3.circ as structural Verilog: 1 circuit, main circuit main
module main (
);

  wire Carry, CLK, clock_1_out, counter_1_carry, D0, D1, D2, D3, Enable, EnQ0_out, EnQ1_out, EnQ2_out, Load,
       multiplexer_1_out, multiplexer_2_out, multiplexer_3_out, multiplexer_4_out, not_1_out, Q0, Q1, Q2, Q3,
       xor_1_out, xor_2_out, xor_3_out, xor_4_out;
  wire [5:1] counter_1_q;

  and EnQ0 (EnQ0_out, Enable, Q0);
  and EnQ1 (EnQ1_out, EnQ0_out, Q1);
  and EnQ2 (EnQ2_out, EnQ1_out, Q2);
  and EnQ3 (Carry, EnQ2_out, Q3);
  xor xor_1 (xor_1_out, Q0, Enable);
  xor xor_2 (xor_2_out, Q1, EnQ0_out);
  xor xor_3 (xor_3_out, Q2, EnQ1_out);
  xor xor_4 (xor_4_out, Q3, EnQ2_out);
  Multiplexer multiplexer_1 (.in0(xor_1_out), .in1(D0), .out(multiplexer_1_out), .sel(Load));  // open: en
  Multiplexer multiplexer_2 (.in0(xor_2_out), .in1(D1), .out(multiplexer_2_out), .sel(Load));  // open: en
  Multiplexer multiplexer_3 (.in0(xor_3_out), .in1(D2), .out(multiplexer_3_out), .sel(Load));  // open: en
  Multiplexer multiplexer_4 (.in0(xor_4_out), .in1(D3), .out(multiplexer_4_out), .sel(Load));  // open: en
  D_Flip_Flop d_ff_1 (.clk(CLK), .D(multiplexer_1_out), .Q(Q0));  // open: Qn, preset, en, reset
  D_Flip_Flop d_ff_2 (.clk(CLK), .D(multiplexer_2_out), .Q(Q1));  // open: Qn, preset, en, reset
  D_Flip_Flop d_ff_3 (.clk(CLK), .D(multiplexer_3_out), .Q(Q2));  // open: Qn, preset, en, reset
  D_Flip_Flop d_ff_4 (.clk(CLK), .D(multiplexer_4_out), .Q(Q3));  // open: Qn, preset, en, reset
  Counter #(.width(6), .max('h24)) counter_1 (
    .Q({counter_1_q[5], Load, D3, counter_1_q[2:1], D0}), .carry(counter_1_carry), .clk(CLK));  // open: load, D, count, clr
  and and_1 (CLK, clock_1_out, not_1_out);
  not not_1 (not_1_out, counter_1_carry);
  Clock clock_1 (.out(clock_1_out));
  TTY #(.rows(1), .cols(37)) tty_1 (.data({2'b10, Carry, Q3, Q2, Q1, Q0}), .clk(CLK));  // open: we, clr
  not not_2 (Enable, counter_1_q[5]);
  or or_1 (D1, Enable, counter_1_q[1]);
  or or_2 (D2, counter_1_q[2], Load);

  // Notes on the sheet:
  //   @ABCDEFGHIJKLMN_@FGFGFGFGN_N_N_N0000
endmodule
