// Logisim project cpu.circ as structural Verilog: 5 circuits, main circuit main
module main (
  output [4:0] out_1,
  output [3:0] out_2,
  output [7:0] out_3,
  output [3:0] out_4,
  output [7:0] out_5,
  output [7:0] out_6,
  output [7:0] out_7,
  output [7:0] out_8
);

  wire CLK, clock_1_out, comparator_1_lt, comparator_2_lt, counter_1_carry, decoder_1_out0, decoder_1_out1,
       decoder_1_out2, decoder_1_out3, decoder_1_out4, decoder_1_out5, decoder_1_out6, decoder_1_out7,
       decoder_1_out8, decoder_1_out15, HALT, NOP, not_1_out, Reset, TClock;
  wire [3:0] B, DEST, multiplexer_3_out, rom_1_data;
  wire [4:0] counter_1_q;
  wire [6:0] adder_1_out, adder_2_out, LSB, MSB;
  wire [7:0] multiplexer_4_out, R1, R2, R3, R4, R5, R6, R7, R8;

  and and_1 (CLK, HALT, TClock);
  PC PC (.CLK(CLK), .Q0(out_1[0]), .Q1(out_1[1]), .Q2(out_1[2]), .Q3(out_1[3]), .Q4(out_1[4]), .reset(Reset));
  RAM #(.addrWidth(5), .dataWidth(24)) ram_1 (
    .addr(out_1), .data({out_2, DEST, out_4, B, out_7}), .clk(CLK));  // open: sel, ld, clr
  Multiplexer #(.select(4), .width(8), .enable("false")) multiplexer_1 (
    .in0(out_3), .in1(R1), .in2(R2), .in3(R3), .in4(R4), .in5(R5), .in6(R6), .in7(R7), .in8(R8), .out(out_6),
    .sel(out_4));  // open: in9, in10, in11, in12, in13, in14, in15
  ALU alu_1 (.RA(out_6), .RB(out_5), .DATA(out_7), .OUTPUT(out_8), .OP(out_2), .NOP(NOP), .HALT(HALT));
  Multiplexer #(.select(4), .width(8), .enable("false")) multiplexer_2 (
    .in0(out_3), .in1(R1), .in2(R2), .in3(R3), .in4(R4), .in5(R5), .in6(R6), .in7(R7), .in8(R8), .out(out_5),
    .sel(B));  // open: in9, in10, in11, in12, in13, in14, in15
  Multiplexer #(.width(4), .enable("false")) multiplexer_3 (
    .in0(DEST), .in1(4'b1111), .out(multiplexer_3_out), .sel(NOP));
  TTY #(.rows(33), .cols(1)) tty_1 (.data(MSB), .clk(TClock), .clr(Reset));  // open: we
  Decoder #(.select(4), .enable("false")) decoder_1 (
    .out0(decoder_1_out0), .out1(decoder_1_out1), .out2(decoder_1_out2), .out3(decoder_1_out3),
    .out4(decoder_1_out4), .out5(decoder_1_out5), .out6(decoder_1_out6), .out7(decoder_1_out7),
    .out8(decoder_1_out8), .out15(decoder_1_out15), .sel(multiplexer_3_out));  // open: out9, out10, out11, out12, out13, out14
  TTY #(.rows(33), .cols(1)) tty_2 (.data(LSB), .clk(TClock), .clr(Reset));  // open: we
  Register register_1 (.IN_star(out_8), .CLK(CLK), .write_enable(decoder_1_out1), .R_star(R1));
  Register register_2 (.IN_star(out_8), .CLK(CLK), .write_enable(decoder_1_out0), .R_star(out_3));
  Button u_Reset (.out(Reset));
  Counter #(.width(5), .max('h1f)) counter_1 (
    .Q(counter_1_q), .carry(counter_1_carry), .clk(TClock), .clr(Reset));  // open: load, D, count
  Register register_3 (.IN_star(out_8), .CLK(CLK), .write_enable(decoder_1_out2), .R_star(R2));
  Multiplexer #(.select(4), .width(8), .disabled(0), .enable("false")) multiplexer_4 (
    .in0(out_3), .in1(R1), .in2(R2), .in3(R3), .in4(R4), .in5(R5), .in6(R6), .in7(R7), .in8(R8),
    .out(multiplexer_4_out), .sel(rom_1_data));  // open: in9, in10, in11, in12, in13, in14, in15
  not not_1 (not_1_out, counter_1_carry);
  Clock clock_1 (.out(clock_1_out));
  Register register_4 (.IN_star(out_8), .CLK(CLK), .write_enable(decoder_1_out3), .R_star(R3));
  and and_2 (TClock, not_1_out, clock_1_out);
  Register register_5 (.IN_star(out_8), .CLK(CLK), .write_enable(decoder_1_out5), .R_star(R5));
  Register register_6 (.IN_star(out_8), .CLK(CLK), .write_enable(decoder_1_out4), .R_star(R4));
  Comparator #(.width(7)) comparator_1 (
    .a(7'b0111001), .b({3'b011, multiplexer_4_out[3:0]}), .lt(comparator_1_lt));  // open: gt, eq
  Comparator #(.width(7)) comparator_2 (
    .a(7'b0111001), .b({3'b011, multiplexer_4_out[7:4]}), .lt(comparator_2_lt));  // open: gt, eq
  ROM #(.addrWidth(5), .dataWidth(4)) rom_1 (.addr(counter_1_q), .data(rom_1_data));  // open: sel
  Register register_7 (.IN_star(out_8), .CLK(CLK), .write_enable(decoder_1_out6), .R_star(R6));
  Adder #(.width(7)) adder_1 (
    .a({3'b011, multiplexer_4_out[3:0]}), .b(7'b0000111), .out(adder_1_out));  // open: cin, cout
  Adder #(.width(7)) adder_2 (
    .a({3'b011, multiplexer_4_out[7:4]}), .b(7'b0000111), .out(adder_2_out));  // open: cin, cout
  Register register_8 (.IN_star(out_8), .CLK(CLK), .write_enable(decoder_1_out7), .R_star(R7));
  Multiplexer #(.width(7), .disabled(0), .enable("false")) multiplexer_5 (
    .in0({3'b011, multiplexer_4_out[3:0]}), .in1(adder_1_out), .out(LSB), .sel(comparator_1_lt));
  Multiplexer #(.width(7), .disabled(0), .enable("false")) multiplexer_6 (
    .in0({3'b011, multiplexer_4_out[7:4]}), .in1(adder_2_out), .out(MSB), .sel(comparator_2_lt));
  Register register_9 (.IN_star(out_8), .CLK(CLK), .write_enable(decoder_1_out8), .R_star(R8));

  // Other names for the same wires on the sheet: DATA[7:0] = out_7; A[3:0] = out_4; OP[3:0] = out_2; IN0[7:0] = out_8;
  //   IN1[7:0] = out_8; IN2[7:0] = out_8; IN3[7:0] = out_8; IN4[7:0] = out_8; IN5[7:0] = out_8; IN6[7:0] = out_8;
  //   IN7[7:0] = out_8; IN8[7:0] = out_8; OUTPUT[7:0] = out_8; R0[7:0] = out_3; RA[7:0] = out_6; RB[7:0] = out_5

  // Notes on the sheet:
  //   00
  //   F5
  //   5A
  //   50
  //   FF
  //   0A
  //   4F
  //   F5
  //   EA
  //   7A
  //   9B
  //   65
  //   0F
  //   FF
  //   F5
  //   AA
  //   5A
  //   0A
  //   FA
  //   A5
  //   04
  //   5A
  //   B4
  //   2D
  //   0A
  //   B0
  //   50
  //   0F
  //   00
  //   00
  //   5A
  //   contents of rom_1 (hex, n*v repeats v):
  //   0 0 1 2 3 4 5 6 7 8 2 3 4 5 0 0 1 6 7 8 2 3 4 5 6 6 7 8 2 3 4 4
endmodule

module PC (
  input  CLK,
  input  reset,
  output Q0,
  output Q1,
  output Q2,
  output Q3,
  output Q4
);

  wire and_1_out, and_2_out, and_3_out;

  T_Flip_Flop t_ff_1 (.clk(CLK), .T(1'b1), .Q(Q0), .reset(reset));  // open: Qn, preset, en
  T_Flip_Flop t_ff_2 (.clk(CLK), .T(Q0), .Q(Q1), .reset(reset));  // open: Qn, preset, en
  and and_1 (and_1_out, Q1, Q0);
  T_Flip_Flop t_ff_3 (.clk(CLK), .T(and_1_out), .Q(Q2), .reset(reset));  // open: Qn, preset, en
  and and_2 (and_2_out, Q2, and_1_out);
  T_Flip_Flop t_ff_4 (.clk(CLK), .T(and_2_out), .Q(Q3), .reset(reset));  // open: Qn, preset, en
  and and_3 (and_3_out, Q3, and_2_out);
  T_Flip_Flop t_ff_5 (.clk(CLK), .T(and_3_out), .Q(Q4), .reset(reset));  // open: Qn, preset, en
  // Probe on {Q4, Q3, Q2, Q1, Q0}
endmodule

// REG
module Register (
  input  CLK,
  input  [7:0] IN_star,
  input  write_enable,
  output [7:0] R_star
);

  D_Flip_Flop d_ff_1 (.clk(CLK), .D(IN_star[0]), .Q(R_star[0]), .en(write_enable));  // open: Qn, preset, reset
  D_Flip_Flop d_ff_2 (.clk(CLK), .D(IN_star[1]), .Q(R_star[1]), .en(write_enable));  // open: Qn, preset, reset
  D_Flip_Flop d_ff_3 (.clk(CLK), .D(IN_star[2]), .Q(R_star[2]), .en(write_enable));  // open: Qn, preset, reset
  D_Flip_Flop d_ff_4 (.clk(CLK), .D(IN_star[3]), .Q(R_star[3]), .en(write_enable));  // open: Qn, preset, reset
  D_Flip_Flop d_ff_5 (.clk(CLK), .D(IN_star[4]), .Q(R_star[4]), .en(write_enable));  // open: Qn, preset, reset
  D_Flip_Flop d_ff_6 (.clk(CLK), .D(IN_star[5]), .Q(R_star[5]), .en(write_enable));  // open: Qn, preset, reset
  D_Flip_Flop d_ff_7 (.clk(CLK), .D(IN_star[6]), .Q(R_star[6]), .en(write_enable));  // open: Qn, preset, reset
  D_Flip_Flop d_ff_8 (.clk(CLK), .D(IN_star[7]), .Q(R_star[7]), .en(write_enable));  // open: Qn, preset, reset
endmodule

module ALU (
  input  [7:0] RB,
  input  [7:0] DATA,
  input  [7:0] RA,
  input  [3:0] OP,
  output NOP,
  output [7:0] OUTPUT,
  output HALT
);

  wire decoder_1_out7, decoder_1_out8, decoder_1_out9, decoder_1_out15, or_1_out, or_2_out;

  Decoder #(.select(4)) decoder_1 (
    .out7(decoder_1_out7), .out8(decoder_1_out8), .out9(decoder_1_out9), .out11(NOP),
    .out15(decoder_1_out15), .sel(OP));  // open: out0, out1, out2, out3, out4, out5, out6, out10, out12, out13, out14, en
  or or_1 (or_1_out, decoder_1_out7, decoder_1_out9);
  or or_2 (or_2_out, decoder_1_out9, decoder_1_out8);
  not not_1 (HALT, decoder_1_out15);
  CLU clu_1 (.CIN(or_1_out), .RB(RB), .DATA(DATA), .IMMED(or_2_out), .RA(RA), .OP(OP), .OUTPUT(OUTPUT));

  // Other names for the same wires on the sheet: A[7:0] = RA; B[7:0] = RB
endmodule

module CLU (
  input  CIN,
  input  [7:0] RB,
  input  [7:0] DATA,
  input  IMMED,
  input  [7:0] RA,
  input  [3:0] OP,
  output [7:0] OUTPUT
);

  wire and_1_out, and_2_out, and_3_out, and_4_out, and_5_out, and_6_out, and_7_out, and_8_out, and_9_out,
       and_10_out, and_11_out, and_12_out, and_13_out, and_14_out, and_15_out, and_16_out, and_17_out,
       and_18_out, and_19_out, and_20_out, CARRY, multiplexer_1_out, multiplexer_2_out, multiplexer_3_out,
       multiplexer_4_out, multiplexer_7_out, multiplexer_8_out, multiplexer_9_out, multiplexer_10_out,
       not_5_out, not_6_out, not_7_out, not_8_out, not_13_out, not_14_out, not_15_out, not_16_out, or_5_out,
       or_6_out, or_7_out, or_8_out, or_13_out, or_14_out, or_15_out, p0_2_out, p0_out, p1_2_out, p1_out,
       p2_2_out, p2_out, p3_2_out, p3_out;
  wire [3:0] multiplexer_5_out, multiplexer_5_out_2, not_4_out, not_9_out;
  wire [7:0] g0_out, or_4_out, xor_2_out;

  not not_1 (not_4_out[1], RA[1]);
  not not_2 (not_4_out[2], RA[2]);
  not not_3 (not_4_out[3], RA[3]);
  not not_4 (not_4_out[0], RA[0]);
  or or_1 (or_4_out[1], RA[1], multiplexer_5_out[1]);
  or or_2 (or_4_out[2], RA[2], multiplexer_5_out[2]);
  or or_3 (or_4_out[3], RA[3], multiplexer_5_out[3]);
  or or_4 (or_4_out[0], RA[0], multiplexer_5_out[0]);
  not not_5 (not_5_out, multiplexer_5_out[2]);
  Multiplexer #(.enable("false")) multiplexer_1 (
    .in0(multiplexer_5_out[3]), .in1(not_6_out), .out(multiplexer_1_out), .sel(CIN));
  not not_6 (not_6_out, multiplexer_5_out[3]);
  Multiplexer #(.enable("false")) multiplexer_2 (
    .in0(multiplexer_5_out[0]), .in1(not_7_out), .out(multiplexer_2_out), .sel(CIN));
  not not_7 (not_7_out, multiplexer_5_out[0]);
  Multiplexer #(.enable("false")) multiplexer_3 (
    .in0(multiplexer_5_out[1]), .in1(not_8_out), .out(multiplexer_3_out), .sel(CIN));
  not not_8 (not_8_out, multiplexer_5_out[1]);
  Multiplexer #(.enable("false")) multiplexer_4 (
    .in0(multiplexer_5_out[2]), .in1(not_5_out), .out(multiplexer_4_out), .sel(CIN));
  and g0 (g0_out[0], RA[0], multiplexer_2_out);
  xor p0 (p0_out, RA[0], multiplexer_2_out);
  and g1 (g0_out[1], RA[1], multiplexer_3_out);
  xor p1 (p1_out, RA[1], multiplexer_3_out);
  and g2 (g0_out[2], RA[2], multiplexer_4_out);
  xor p2 (p2_out, RA[2], multiplexer_4_out);
  and g3 (g0_out[3], RA[3], multiplexer_1_out);
  xor p3 (p3_out, RA[3], multiplexer_1_out);
  and and_1 (and_1_out, CIN, p0_out);
  and and_2 (and_2_out, p1_out, g0_out[0]);
  and and_3 (and_3_out, p1_out, p0_out, CIN);
  and and_4 (and_4_out, p2_out, g0_out[1]);
  and and_5 (and_5_out, g0_out[0], p1_out, p2_out);
  and and_6 (and_6_out, p3_out, g0_out[2]);
  and and_7 (and_7_out, p3_out, p2_out, g0_out[1]);
  or or_5 (or_5_out, g0_out[0], and_1_out);
  or or_6 (or_6_out, and_2_out, and_3_out, g0_out[1]);
  and and_8 (and_8_out, p0_out, p1_out, p2_out, CIN);
  and and_9 (and_9_out, p3_out, p2_out, p1_out, g0_out[0]);
  and and_10 (and_10_out, p3_out, p2_out, CIN, p1_out, p0_out);
  or or_7 (or_7_out, g0_out[2], and_4_out, and_5_out, and_8_out);
  xor xor_1 (xor_2_out[3], or_7_out, p3_out);
  or or_8 (or_8_out, g0_out[3], and_6_out, and_7_out, and_9_out, and_10_out);
  xor xor_2 (xor_2_out[0], p0_out, CIN);
  xor xor_3 (xor_2_out[1], or_5_out, p1_out);
  xor xor_4 (xor_2_out[2], or_6_out, p2_out);
  Multiplexer #(.width(8), .enable("false")) multiplexer_5 (
    .in0(RB), .in1(DATA), .out({multiplexer_5_out_2, multiplexer_5_out}), .sel(IMMED));
  not not_9 (not_9_out[0], RA[4]);
  not not_10 (not_9_out[1], RA[5]);
  not not_11 (not_9_out[2], RA[6]);
  not not_12 (not_9_out[3], RA[7]);
  Multiplexer #(.select(4), .width(8), .enable("false")) multiplexer_6 (
    .in0(g0_out), .in1(or_4_out), .in2({not_9_out, not_4_out}), .in3(xor_2_out), .in4(RA),
    .in5({RA[6:0], 1'b0}), .in6({1'b0, RA[7:1]}), .in7(xor_2_out), .in8(xor_2_out), .in9(xor_2_out),
    .in10(DATA), .out(OUTPUT), .sel(OP));  // open: in11, in12, in13, in14, in15
  or or_9 (or_4_out[4], RA[4], multiplexer_5_out_2[0]);
  or or_10 (or_4_out[5], multiplexer_5_out_2[1], RA[5]);
  or or_11 (or_4_out[6], multiplexer_5_out_2[2], RA[6]);
  or or_12 (or_4_out[7], multiplexer_5_out_2[3], RA[7]);
  not not_13 (not_13_out, multiplexer_5_out_2[1]);
  not not_14 (not_14_out, multiplexer_5_out_2[2]);
  Multiplexer #(.enable("false")) multiplexer_7 (
    .in0(multiplexer_5_out_2[3]), .in1(not_15_out), .out(multiplexer_7_out), .sel(CIN));
  not not_15 (not_15_out, multiplexer_5_out_2[3]);
  Multiplexer #(.enable("false")) multiplexer_8 (
    .in0(multiplexer_5_out_2[0]), .in1(not_16_out), .out(multiplexer_8_out), .sel(CIN));
  not not_16 (not_16_out, multiplexer_5_out_2[0]);
  Multiplexer #(.enable("false")) multiplexer_9 (
    .in0(multiplexer_5_out_2[1]), .in1(not_13_out), .out(multiplexer_9_out), .sel(CIN));
  Multiplexer #(.enable("false")) multiplexer_10 (
    .in0(multiplexer_5_out_2[2]), .in1(not_14_out), .out(multiplexer_10_out), .sel(CIN));
  and g0_2 (g0_out[4], RA[4], multiplexer_8_out);
  xor p0_2 (p0_2_out, RA[4], multiplexer_8_out);
  and g1_2 (g0_out[5], RA[5], multiplexer_9_out);
  xor p1_2 (p1_2_out, RA[5], multiplexer_9_out);
  and g2_2 (g0_out[6], RA[6], multiplexer_10_out);
  xor p2_2 (p2_2_out, RA[6], multiplexer_10_out);
  and g3_2 (g0_out[7], RA[7], multiplexer_7_out);
  xor p3_2 (p3_2_out, RA[7], multiplexer_7_out);
  and and_11 (and_11_out, or_8_out, p0_2_out);
  and and_12 (and_12_out, p1_2_out, g0_out[4]);
  and and_13 (and_13_out, p1_2_out, p0_2_out, or_8_out);
  and and_14 (and_14_out, p2_2_out, g0_out[5]);
  and and_15 (and_15_out, g0_out[4], p1_2_out, p2_2_out);
  and and_16 (and_16_out, p0_2_out, p1_2_out, p2_2_out, or_8_out);
  and and_17 (and_17_out, p3_2_out, g0_out[6]);
  and and_18 (and_18_out, p3_2_out, p2_2_out, g0_out[5]);
  and and_19 (and_19_out, p3_2_out, p2_2_out, p1_2_out, g0_out[4]);
  and and_20 (and_20_out, p3_2_out, p2_2_out, or_8_out, p1_2_out, p0_2_out);
  or or_13 (or_13_out, g0_out[4], and_11_out);
  or or_14 (or_14_out, and_12_out, and_13_out, g0_out[5]);
  or or_15 (or_15_out, g0_out[6], and_14_out, and_15_out, and_16_out);
  xor xor_5 (xor_2_out[5], or_13_out, p1_2_out);
  xor xor_6 (xor_2_out[6], or_14_out, p2_2_out);
  xor xor_7 (xor_2_out[7], or_15_out, p3_2_out);
  or or_16 (CARRY, g0_out[7], and_17_out, and_18_out, and_19_out, and_20_out);
  xor xor_8 (xor_2_out[4], p0_2_out, or_8_out);
endmodule
